# Fritzing sketch RobotDiagram (saved by Fritzing 0.9.10b)

parts:
  Part1 = Adafruit LSM303DLHC Triple-axis Accelerometer+Magnetometer (Compass) [part_number="Adafruit #1120"]
  Part3 = GY-VL53L0XV2 Laser Ranger Module
  L298N1 = L298N DC motor driver
  M1 = DC Motor [part_number="12V DC Motor" voltage_(max)=12V voltage_(min)=3V]
  M2 = DC Motor [part_number="12V DC Motor" voltage_(max)=12V voltage_(min)=3V]
  A1 = Arduino UNO R4 WiFi

nets:
  N1: Part1.SCL, Part3.SCL, A1.Pin_51
  N2: Part1.SDA, Part3.SDA, A1.Pin_50
  GND: Part1.GND, Part3.GND, A1.Pin_10, A1.Pin_48
  3.3V: Part1.3.3V, Part3.VCC, A1.Pin_7
  N3: L298N1.OUT1, M1.pin_1
  N4: L298N1.OUT2, M1.pin_2
  N5: L298N1.OUT3, M2.pin_2
  N6: L298N1.OUT4, M2.pin_1
  N7: L298N1.ENA, A1.Pin_43
  N8: L298N1.ENB, A1.Pin_37
  N9: L298N1.IN1, A1.Pin_42
  N10: L298N1.IN2, A1.Pin_41
  N11: L298N1.IN3, A1.Pin_38
  N12: L298N1.IN4, A1.Pin_39

notes:
  12v battery
  Notice the crossed wires.
  L298N
  Motor Controller
  D3->ENB
  D4->IN1B
  D5->IN2B
  D7->IN1A
  D8->IN2A
  D9->ENA
  LSM303DLHC 3V
  Compass+Accel
  SCL->SCL
  SDA->SDA
  CJVL53L0XV2 3V
  Distance
  SCL->SCL
  SDA->SDA

custom parts:
  Adafruit LSM303DLHC Triple-axis Accelerometer+Magnetometer (Compass): He told you "Go West, young maker!" - but you don't know which way is West! Ah, if only you had this triple-axis accelerometer/magnetometer compass module. Inside are two sensors, one is a classic 3-axis accelerometer, which can tell you which direction is down towards the Earth (by measuring gravity). The other is a magnetometer that can sense where the strongest magnetic force is coming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
  GY-VL53L0XV2 Laser Ranger Module: The GY-VL53L0XV2 is based on the VL53L0X from ST Microelectronics, a time-of-flight ranging system integrated into a compact module.
  L298N DC motor driver: 2x DC motor driver with 78M05 positive voltage regulator (7..35 V) L298N: max 46 V, 2 A Set 5 V Enable jumper to enable 5 V regultor (needed for the L298N) and +5 V output at screw terminal or supply external +5 V at screw terminal Set ENA and/or ENB to +5 V to enable motor permanently or supply ENA and/or ENB with PWM signal IN1 and IN2 set rotation directory for motor A (OUT1/OUT2) IN2 and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
  Arduino UNO R4 WiFi: The Arduino UNO R4 WiFi merges the RA4M1 microprocessor from Renesas with the ESP32-S3 from Espressif, creating an all-in-one tool for makers with enhanced processing power and a diverse array of new peripherals.

// code stored in the sketch: SmartRobot03.ino
// I
// S
// M-FF+FF
//
#include <L298NX2.h>
const unsigned int EN_A  = 9,
                   IN1_A = 8,
                   IN2_A = 7,
                  
                   IN1_B = 4,
                   IN2_B = 5,
                   EN_B  = 3;
                   
int                lPower = 0, 
                   rPower = 0;

// Initialize both motors
L298NX2                       motors(EN_A, IN1_A, IN2_A, EN_B, IN1_B, IN2_B);

// Distance sensor
#include <VL53L0X.h>
VL53L0X                        distance;
float                          currentDistanceInCentimeters = 0;

#include <Adafruit_Sensor.h>

// Accellerator
#include <Adafruit_LSM303_Accel.h>
Adafruit_LSM303_Accel_Unified  accel   = Adafruit_LSM303_Accel_Unified(54321);
bool                           accelOK = false;

// Compass / Magnet sensor
#include <Adafruit_LSM303DLH_Mag.h>
Adafruit_LSM303DLH_Mag_Unified mag     = Adafruit_LSM303DLH_Mag_Unified(12345);
bool                           magOK   = false;

void controlMotors(int l, int r)
{
  lPower = l; rPower = r;
  if (l == 0 && r == 0)
  {
    motors.stop();
    return;
  }

  (l > 0) ?  motors.forwardA() : motors.backwardA();
  motors.setSpeedA(abs(l));
    
  (r > 0) ? motors.forwardB() : motors.backwardB();
  motors.setSpeedB(abs(r));  
}

void stop()
{
  controlMotors(0, 0);
}

float getCompassHeading()
{
  if (!magOK)
  {
    return -1.0;
  }
  sensors_event_t event;
  mag.getEvent(&event);
 
  float heading = (atan2(event.magnetic.y,event.magnetic.x) * 180) / 3.14159;
  if (abs(heading) < 0.1)
  {
    mag.getEvent(&event);
    heading = (atan2(event.magnetic.y,event.magnetic.x) * 180) / 3.14159; 
  }
  
  if (heading < 0)
  {
    heading = 360 + heading;
  }

  heading = round(heading);
  return heading;
}


void sendSensorValues()
{
  String sensorValues = "";
  if (accelOK)
  {
    sensors_event_t event;
    accel.getEvent(&event);
    sensorValues += "X" + String(event.acceleration.x, 1);
    sensorValues += "Y" + String(event.acceleration.y, 1);
    sensorValues += "Z" + String(event.acceleration.z, 1);
  }

  if (magOK)
  {
    sensorValues += "M" + String(getCompassHeading(), 1);
  }

  sensorValues += "D" + String(currentDistanceInCentimeters);
  sensorValues += "L" + String(lPower);
  sensorValues += "R" + String(rPower);

  sensorValues += ";";

   Serial.println(sensorValues);
}

void initializeDistance()
{
  Wire.begin();

  distance.init();
  distance.setTimeout(500);
  distance.startContinuous();
}


void initializeMag()
{
  mag.enableAutoRange(true);
  magOK   = mag.begin();
}

void initializeAccel()
{
  accelOK = accel.begin();

  if (accelOK)
  {
    accel.setRange(LSM303_RANGE_4G);
  }
}


// Converts a hex number in the format +FF or -FF to integer.
int xtoi(String s, int start)
{
  int signal = s[start] == '+' ? 1 : -1;
  start++;
  int tens   = (s[start] < '9') ? s[start] - '0' : s[start] - '7';
  start++;
  int ones   = (s[start] < '9') ? s[start] - '0' : s[start] - '7';

  return (tens * 16) + ones;
}

void setup() 
{
  Serial.begin(115200);
  Serial.println("Starting...");  
  initializeDistance();
  Serial.println("1");  

  initializeMag();
  Serial.println("2");  
  initializeAccel();

  Serial.println("3");  
  stop();
  Serial.println("Device is ready 20220507 1525");  
  Serial.println("Accepted commands: See comments at top of this source code.");  
}

void loop() 
{
  currentDistanceInCentimeters = distance.readRangeContinuousMillimeters() / 10; 
  if (currentDistanceInCentimeters < 15 && (lPower != 0 || rPower != 0))
  {
    controlMotors(0, 0);
  }  

  if (Serial.available() > 0)
  {
    String s = Serial.readStringUntil('\n');
    s.toUpperCase();
    switch (s[0])
    {
      case 'I':
        Serial.println("SmartRobot03.");
        break;        
      case 'M':
        lPower = xtoi(s, 1);
        rPower = xtoi(s, 4);
        controlMotors(lPower, rPower);
        // yes, I want to fall through to get sensor.
      case 'S':
        sendSensorValues();
        break;
    }
  }
}
